// Logisim project riscv_simulator_multibus.circ as structural Verilog: 3 circuits, main circuit main
module main (
  input  in_1,
  input  in_2,
  input  in_3,
  input  in_4,
  input  in_5,
  input  in_6,
  input  in_7,
  input  in_8,
  input  in_9,
  input  in_10,
  output [31:0] out_11,
  output [31:0] out_12,
  output [6:0] out_13,
  output [31:0] out_14,
  output [31:0] out_15,
  output [31:0] out_16
);

  wire clock_2_out, clock_3_out, clock_4_out, clock_5_out, comparator_1_eq, comparator_2_eq, comparator_3_eq,
       comparator_4_eq, comparator_5_eq, comparator_6_eq, comparator_7_eq, comparator_8_eq, comparator_9_eq,
       comparator_10_eq, not_1_out, or_1_out, or_2_out, or_3_out, undriven_2;
  wire [2:0] decoder_2_out5, decoder_2_out13, decoder_2_out21, decoder_2_out29, decoder_3_out13,
       decoder_3_out21, decoder_3_out29, fd_1_format, priority_encoder_1_out;
  wire [4:0] decoder_2_out0, decoder_2_out8, decoder_2_out16, decoder_2_out24, decoder_3_out8,
       decoder_3_out16, decoder_3_out24, rd0, WB_rd;
  wire [6:0] op0;
  wire [7:0] decoder_3_out0, PC0_q_2;
  wire [9:0] funct;
  wire [23:0] PC0_q;
  wire [31:0] adder_1_out, bit_extender_1_out, bit_extender_2_out, bit_extender_3_out, bit_extender_4_out,
       controlled_buffer_1_out, controlled_buffer_2_out, imm, InstrCache_data, Main_ALU_alu_out,
       multiplexer_1_out, multiplexer_2_out, multiplexer_3_out, multiplexer_4_out, PC1, PC2, PC3, S1, S2, SB,
       undriven, undriven_3, x1_q, x2_q, x3_q, x4_q, x5_q, x6_q, x7_q, x8_q, x9_q, x10_q, x11_q, x12_q,
       x13_q, x14_q, x15_q, x16_q, x17_q, x18_q, x19_q, x20_q, x21_q, x22_q, x23_q, x24_q, x25_q, x26_q,
       x27_q, x28_q, x29_q, x30_q, x31_q;
  wire [31:1] decoder_1_out1;

  Clock clock_1 ();  // open: out
  not not_1 (not_1_out, in_2);
  or or_1 (or_1_out, in_2, in_5);
  Clock clock_2 (.out(clock_2_out));
  Multiplexer #(.width(32)) multiplexer_1 (.in0(adder_1_out), .in1(undriven), .out(multiplexer_1_out), .sel(in_3));
  Register #(.trigger("falling"), .width(32)) u_PC1 (
    .D({PC0_q_2, PC0_q}), .en(1'b1), .clk(clock_2_out), .Q(PC1));  // open: clr
  Register #(.width(32)) PC0 (
    .D(multiplexer_2_out), .en(or_1_out), .clk(clock_2_out), .Q({PC0_q_2, PC0_q}));  // open: clr
  Multiplexer #(.width(32)) multiplexer_2 (
    .in0(32'hdeadbeef), .in1(multiplexer_1_out), .out(multiplexer_2_out), .sel(not_1_out));
  Adder #(.width(32)) adder_1 (.a(32'h4), .b({PC0_q_2, PC0_q}), .out(adder_1_out));  // open: cin, cout
  ROM #(.addrWidth(24), .dataWidth(32)) InstrCache (.addr(PC0_q), .data(InstrCache_data));
  FD fd_1 (.opcode(op0), .format(fd_1_format));
  Multiplexer #(.width(32)) multiplexer_3 (.in0(imm), .in1(S2), .out(multiplexer_3_out), .sel(comparator_1_eq));
  Comparator #(.width(3)) comparator_1 (.a(fd_1_format), .b(3'b001), .eq(comparator_1_eq));  // open: gt, lt
  ALU TA_ALU (.A(imm), .B(PC2), .OP(3'b100));  // open: ALU_OUT, CNZV
  ALU Main_ALU (.A(multiplexer_3_out), .B(S1), .ALU_OUT(Main_ALU_alu_out));  // open: OP, CNZV
  Comparator #(.width(7)) comparator_2 (.a(out_12[6:0]), .b(7'b0110011), .eq(comparator_2_eq));  // open: gt, lt
  Comparator #(.width(7)) comparator_3 (.a(out_12[6:0]), .b(7'b0010011), .eq(comparator_3_eq));  // open: gt, lt
  or or_2 (or_2_out, comparator_3_eq, comparator_4_eq, comparator_5_eq);
  Comparator #(.width(7)) comparator_4 (.a(out_12[6:0]), .b(7'b0000011), .eq(comparator_4_eq));  // open: gt, lt
  Comparator #(.width(7)) comparator_5 (.a(out_12[6:0]), .b(7'b1100111), .eq(comparator_5_eq));  // open: gt, lt
  Comparator #(.width(7)) comparator_6 (.a(out_12[6:0]), .b(7'b0100011), .eq(comparator_6_eq));  // open: gt, lt
  Comparator #(.width(7)) comparator_7 (.a(out_12[6:0]), .b(7'b1100011), .eq(comparator_7_eq));  // open: gt, lt
  Comparator #(.width(7)) comparator_8 (.a(out_12[6:0]), .b(7'b0110111), .eq(comparator_8_eq));  // open: gt, lt
  or or_3 (or_3_out, comparator_8_eq, comparator_9_eq);
  Comparator #(.width(7)) comparator_9 (.a(out_12[6:0]), .b(7'b0010111), .eq(comparator_9_eq));  // open: gt, lt
  Comparator #(.width(7)) comparator_10 (.a(out_12[6:0]), .b(7'b1101111), .eq(comparator_10_eq));  // open: gt, lt
  Register #(.trigger("falling"), .width(32)) u_PC3 (.D(PC2), .en(1'b1), .clk(undriven_2), .Q(PC3));  // open: clr
  Register #(.trigger("falling"), .width(32)) TA (.en(1'b1), .clk(undriven_2));  // open: D, Q, clr
  Register #(.trigger("falling"), .width(32)) aluR (.D(Main_ALU_alu_out), .en(1'b1), .clk(undriven_2));  // open: Q, clr
  Register #(.trigger("falling"), .width(32)) u_SB (.D(S2), .en(1'b1), .clk(undriven_2), .Q(SB));  // open: clr
  Multiplexer #(.width(32)) multiplexer_4 (
    .in0(InstrCache_data), .in1(32'hdeadbeef), .out(multiplexer_4_out), .sel(in_1));
  Priority_Encoder priority_encoder_1 (
    .in0(comparator_2_eq), .in1(or_2_out), .in2(comparator_6_eq), .in3(comparator_7_eq), .in4(or_3_out),
    .in5(comparator_10_eq), .out(priority_encoder_1_out));  // open: in6, in7, en_in, gs, en_out
  Register #(.trigger("falling"), .width(32)) IR (
    .D(multiplexer_4_out), .en(1'b1), .clk(clock_3_out), .Q(out_12), .clr(in_2));
  Clock clock_3 (.out(clock_3_out));
  assign bit_extender_1_out = {{20{out_12[31]}}, out_12[31:20]};  // Bit_Extender bit_extender_1
  assign bit_extender_2_out = {{20{out_12[31]}}, {out_12[31:25], out_12[11:7]}};  // Bit_Extender bit_extender_2
  Multiplexer #(.select(3), .width(32)) multiplexer_5 (
    .in1(bit_extender_1_out), .in2(bit_extender_2_out), .in3(bit_extender_3_out),
    .in4({out_12[31:12], {12{1'b0}}}), .in5(bit_extender_4_out), .out(out_14));  // open: in0, in6, in7, sel
  assign bit_extender_3_out = {{19{out_12[31]}}, {out_12[31], out_12[7], out_12[30:25], out_12[11:8], 1'b0}};  // Bit_Extender bit_extender_3
  assign bit_extender_4_out = {{11{out_12[31]}}, {out_12[31], out_12[19:12], out_12[20], out_12[30:21], 1'b0}};  // Bit_Extender bit_extender_4
  Decoder #(.select(5)) decoder_1 (
    .out1(decoder_1_out1[1]), .out2(decoder_1_out1[2]), .out3(decoder_1_out1[3]), .out4(decoder_1_out1[4]),
    .out5(decoder_1_out1[5]), .out6(decoder_1_out1[6]), .out7(decoder_1_out1[7]), .out8(decoder_1_out1[8]),
    .out9(decoder_1_out1[9]), .out10(decoder_1_out1[10]), .out11(decoder_1_out1[11]),
    .out12(decoder_1_out1[12]), .out13(decoder_1_out1[13]), .out14(decoder_1_out1[14]),
    .out15(decoder_1_out1[15]), .out16(decoder_1_out1[16]), .out17(decoder_1_out1[17]),
    .out18(decoder_1_out1[18]), .out19(decoder_1_out1[19]), .out20(decoder_1_out1[20]),
    .out21(decoder_1_out1[21]), .out22(decoder_1_out1[22]), .out23(decoder_1_out1[23]),
    .out24(decoder_1_out1[24]), .out25(decoder_1_out1[25]), .out26(decoder_1_out1[26]),
    .out27(decoder_1_out1[27]), .out28(decoder_1_out1[28]), .out29(decoder_1_out1[29]),
    .out30(decoder_1_out1[30]), .out31(decoder_1_out1[31]), .sel(WB_rd));  // open: out0, en
  Clock clock_4 (.out(clock_4_out));
  Register #(.width(32)) x1 (.D(undriven_3), .en(decoder_1_out1[1]), .clk(clock_4_out), .Q(x1_q));  // open: clr
  Register #(.width(32)) x2 (.D(undriven_3), .en(decoder_1_out1[2]), .clk(clock_4_out), .Q(x2_q));  // open: clr
  Register #(.width(32)) x3 (.D(undriven_3), .en(decoder_1_out1[3]), .clk(clock_4_out), .Q(x3_q));  // open: clr
  Register #(.width(32)) x4 (.D(undriven_3), .en(decoder_1_out1[4]), .clk(clock_4_out), .Q(x4_q));  // open: clr
  Register #(.width(32)) x5 (.D(undriven_3), .en(decoder_1_out1[5]), .clk(clock_4_out), .Q(x5_q));  // open: clr
  Register #(.width(32)) x6 (.D(undriven_3), .en(decoder_1_out1[6]), .clk(clock_4_out), .Q(x6_q));  // open: clr
  Register #(.width(32)) x7 (.D(undriven_3), .en(decoder_1_out1[7]), .clk(clock_4_out), .Q(x7_q));  // open: clr
  assign controlled_buffer_1_out = decoder_2_out0[0] ? {32{1'b0}} : 32'bz;  // Controlled_Buffer controlled_buffer_1
  assign controlled_buffer_2_out = decoder_3_out0[0] ? {32{1'b0}} : 32'bz;  // Controlled_Buffer controlled_buffer_2
  assign controlled_buffer_1_out = decoder_2_out0[1] ? x1_q : 32'bz;  // Controlled_Buffer controlled_buffer_3
  assign controlled_buffer_2_out = decoder_3_out0[1] ? x1_q : 32'bz;  // Controlled_Buffer controlled_buffer_4
  assign controlled_buffer_1_out = decoder_2_out0[2] ? x2_q : 32'bz;  // Controlled_Buffer controlled_buffer_5
  assign controlled_buffer_2_out = decoder_3_out0[2] ? x2_q : 32'bz;  // Controlled_Buffer controlled_buffer_6
  assign controlled_buffer_1_out = decoder_2_out0[3] ? x3_q : 32'bz;  // Controlled_Buffer controlled_buffer_7
  assign controlled_buffer_2_out = decoder_3_out0[3] ? x3_q : 32'bz;  // Controlled_Buffer controlled_buffer_8
  assign controlled_buffer_1_out = decoder_2_out0[4] ? x4_q : 32'bz;  // Controlled_Buffer controlled_buffer_9
  assign controlled_buffer_2_out = decoder_3_out0[4] ? x4_q : 32'bz;  // Controlled_Buffer controlled_buffer_10
  assign controlled_buffer_1_out = decoder_2_out5[0] ? x5_q : 32'bz;  // Controlled_Buffer controlled_buffer_11
  assign controlled_buffer_2_out = decoder_3_out0[5] ? x5_q : 32'bz;  // Controlled_Buffer controlled_buffer_12
  assign controlled_buffer_1_out = decoder_2_out5[1] ? x6_q : 32'bz;  // Controlled_Buffer controlled_buffer_13
  assign controlled_buffer_2_out = decoder_3_out0[6] ? x6_q : 32'bz;  // Controlled_Buffer controlled_buffer_14
  assign controlled_buffer_1_out = decoder_2_out5[2] ? x7_q : 32'bz;  // Controlled_Buffer controlled_buffer_15
  assign controlled_buffer_2_out = decoder_3_out0[7] ? x7_q : 32'bz;  // Controlled_Buffer controlled_buffer_16
  Register #(.width(32)) x8 (.D(undriven_3), .en(decoder_1_out1[8]), .clk(clock_4_out), .Q(x8_q));  // open: clr
  Register #(.width(32)) x9 (.D(undriven_3), .en(decoder_1_out1[9]), .clk(clock_4_out), .Q(x9_q));  // open: clr
  Register #(.width(32)) x10 (.D(undriven_3), .en(decoder_1_out1[10]), .clk(clock_4_out), .Q(x10_q));  // open: clr
  Register #(.width(32)) x11 (.D(undriven_3), .en(decoder_1_out1[11]), .clk(clock_4_out), .Q(x11_q));  // open: clr
  Register #(.width(32)) x12 (.D(undriven_3), .en(decoder_1_out1[12]), .clk(clock_4_out), .Q(x12_q));  // open: clr
  Register #(.width(32)) x13 (.D(undriven_3), .en(decoder_1_out1[13]), .clk(clock_4_out), .Q(x13_q));  // open: clr
  Register #(.width(32)) x14 (.D(undriven_3), .en(decoder_1_out1[14]), .clk(clock_4_out), .Q(x14_q));  // open: clr
  Register #(.width(32)) x15 (.D(undriven_3), .en(decoder_1_out1[15]), .clk(clock_4_out), .Q(x15_q));  // open: clr
  assign controlled_buffer_1_out = decoder_2_out8[0] ? x8_q : 32'bz;  // Controlled_Buffer controlled_buffer_17
  assign controlled_buffer_1_out = decoder_2_out8[1] ? x9_q : 32'bz;  // Controlled_Buffer controlled_buffer_18
  assign controlled_buffer_1_out = decoder_2_out8[2] ? x10_q : 32'bz;  // Controlled_Buffer controlled_buffer_19
  assign controlled_buffer_1_out = decoder_2_out8[3] ? x11_q : 32'bz;  // Controlled_Buffer controlled_buffer_20
  assign controlled_buffer_1_out = decoder_2_out8[4] ? x12_q : 32'bz;  // Controlled_Buffer controlled_buffer_21
  assign controlled_buffer_1_out = decoder_2_out13[0] ? x13_q : 32'bz;  // Controlled_Buffer controlled_buffer_22
  assign controlled_buffer_1_out = decoder_2_out13[1] ? x14_q : 32'bz;  // Controlled_Buffer controlled_buffer_23
  assign controlled_buffer_1_out = decoder_2_out13[2] ? x15_q : 32'bz;  // Controlled_Buffer controlled_buffer_24
  assign controlled_buffer_2_out = decoder_3_out8[0] ? x8_q : 32'bz;  // Controlled_Buffer controlled_buffer_25
  assign controlled_buffer_2_out = decoder_3_out8[1] ? x9_q : 32'bz;  // Controlled_Buffer controlled_buffer_26
  assign controlled_buffer_2_out = decoder_3_out8[2] ? x10_q : 32'bz;  // Controlled_Buffer controlled_buffer_27
  assign controlled_buffer_2_out = decoder_3_out8[3] ? x11_q : 32'bz;  // Controlled_Buffer controlled_buffer_28
  assign controlled_buffer_2_out = decoder_3_out8[4] ? x12_q : 32'bz;  // Controlled_Buffer controlled_buffer_29
  assign controlled_buffer_2_out = decoder_3_out13[0] ? x13_q : 32'bz;  // Controlled_Buffer controlled_buffer_30
  assign controlled_buffer_2_out = decoder_3_out13[1] ? x14_q : 32'bz;  // Controlled_Buffer controlled_buffer_31
  assign controlled_buffer_2_out = decoder_3_out13[2] ? x15_q : 32'bz;  // Controlled_Buffer controlled_buffer_32
  Register #(.width(32)) x16 (.D(undriven_3), .en(decoder_1_out1[16]), .clk(clock_4_out), .Q(x16_q));  // open: clr
  Register #(.width(32)) x17 (.D(undriven_3), .en(decoder_1_out1[17]), .clk(clock_4_out), .Q(x17_q));  // open: clr
  Register #(.width(32)) x18 (.D(undriven_3), .en(decoder_1_out1[18]), .clk(clock_4_out), .Q(x18_q));  // open: clr
  Register #(.width(32)) x19 (.D(undriven_3), .en(decoder_1_out1[19]), .clk(clock_4_out), .Q(x19_q));  // open: clr
  Register #(.width(32)) x20 (.D(undriven_3), .en(decoder_1_out1[20]), .clk(clock_4_out), .Q(x20_q));  // open: clr
  Register #(.width(32)) x21 (.D(undriven_3), .en(decoder_1_out1[21]), .clk(clock_4_out), .Q(x21_q));  // open: clr
  Register #(.width(32)) x22 (.D(undriven_3), .en(decoder_1_out1[22]), .clk(clock_4_out), .Q(x22_q));  // open: clr
  Register #(.width(32)) x23 (.D(undriven_3), .en(decoder_1_out1[23]), .clk(clock_4_out), .Q(x23_q));  // open: clr
  assign controlled_buffer_1_out = decoder_2_out16[0] ? x16_q : 32'bz;  // Controlled_Buffer controlled_buffer_33
  assign controlled_buffer_2_out = decoder_3_out16[0] ? x16_q : 32'bz;  // Controlled_Buffer controlled_buffer_34
  assign controlled_buffer_1_out = decoder_2_out16[1] ? x17_q : 32'bz;  // Controlled_Buffer controlled_buffer_35
  assign controlled_buffer_2_out = decoder_3_out16[1] ? x17_q : 32'bz;  // Controlled_Buffer controlled_buffer_36
  assign controlled_buffer_1_out = decoder_2_out16[2] ? x18_q : 32'bz;  // Controlled_Buffer controlled_buffer_37
  assign controlled_buffer_2_out = decoder_3_out16[2] ? x18_q : 32'bz;  // Controlled_Buffer controlled_buffer_38
  assign controlled_buffer_1_out = decoder_2_out16[3] ? x19_q : 32'bz;  // Controlled_Buffer controlled_buffer_39
  assign controlled_buffer_2_out = decoder_3_out16[3] ? x19_q : 32'bz;  // Controlled_Buffer controlled_buffer_40
  assign controlled_buffer_1_out = decoder_2_out16[4] ? x20_q : 32'bz;  // Controlled_Buffer controlled_buffer_41
  assign controlled_buffer_2_out = decoder_3_out16[4] ? x20_q : 32'bz;  // Controlled_Buffer controlled_buffer_42
  assign controlled_buffer_1_out = decoder_2_out21[0] ? x21_q : 32'bz;  // Controlled_Buffer controlled_buffer_43
  assign controlled_buffer_2_out = decoder_3_out21[0] ? x21_q : 32'bz;  // Controlled_Buffer controlled_buffer_44
  assign controlled_buffer_1_out = decoder_2_out21[1] ? x22_q : 32'bz;  // Controlled_Buffer controlled_buffer_45
  assign controlled_buffer_2_out = decoder_3_out21[1] ? x22_q : 32'bz;  // Controlled_Buffer controlled_buffer_46
  assign controlled_buffer_1_out = decoder_2_out21[2] ? x23_q : 32'bz;  // Controlled_Buffer controlled_buffer_47
  assign controlled_buffer_2_out = decoder_3_out21[2] ? x23_q : 32'bz;  // Controlled_Buffer controlled_buffer_48
  Register #(.width(32)) x24 (.D(undriven_3), .en(decoder_1_out1[24]), .clk(clock_4_out), .Q(x24_q));  // open: clr
  Register #(.width(32)) x25 (.D(undriven_3), .en(decoder_1_out1[25]), .clk(clock_4_out), .Q(x25_q));  // open: clr
  Register #(.width(32)) x26 (.D(undriven_3), .en(decoder_1_out1[26]), .clk(clock_4_out), .Q(x26_q));  // open: clr
  Register #(.width(32)) x27 (.D(undriven_3), .en(decoder_1_out1[27]), .clk(clock_4_out), .Q(x27_q));  // open: clr
  Register #(.width(32)) x28 (.D(undriven_3), .en(decoder_1_out1[28]), .clk(clock_4_out), .Q(x28_q));  // open: clr
  Register #(.width(32)) x29 (.D(undriven_3), .en(decoder_1_out1[29]), .clk(clock_4_out), .Q(x29_q));  // open: clr
  Register #(.width(32)) x30 (.D(undriven_3), .en(decoder_1_out1[30]), .clk(clock_4_out), .Q(x30_q));  // open: clr
  Register #(.width(32)) x31 (.D(undriven_3), .en(decoder_1_out1[31]), .clk(clock_4_out), .Q(x31_q));  // open: clr
  assign controlled_buffer_1_out = decoder_2_out24[0] ? x24_q : 32'bz;  // Controlled_Buffer controlled_buffer_49
  assign controlled_buffer_2_out = decoder_3_out24[0] ? x24_q : 32'bz;  // Controlled_Buffer controlled_buffer_50
  assign controlled_buffer_1_out = decoder_2_out24[1] ? x25_q : 32'bz;  // Controlled_Buffer controlled_buffer_51
  assign controlled_buffer_2_out = decoder_3_out24[1] ? x25_q : 32'bz;  // Controlled_Buffer controlled_buffer_52
  assign controlled_buffer_1_out = decoder_2_out24[2] ? x26_q : 32'bz;  // Controlled_Buffer controlled_buffer_53
  assign controlled_buffer_2_out = decoder_3_out24[2] ? x26_q : 32'bz;  // Controlled_Buffer controlled_buffer_54
  assign controlled_buffer_1_out = decoder_2_out24[3] ? x27_q : 32'bz;  // Controlled_Buffer controlled_buffer_55
  assign controlled_buffer_2_out = decoder_3_out24[3] ? x27_q : 32'bz;  // Controlled_Buffer controlled_buffer_56
  assign controlled_buffer_1_out = decoder_2_out24[4] ? x28_q : 32'bz;  // Controlled_Buffer controlled_buffer_57
  assign controlled_buffer_2_out = decoder_3_out24[4] ? x28_q : 32'bz;  // Controlled_Buffer controlled_buffer_58
  assign controlled_buffer_1_out = decoder_2_out29[0] ? x29_q : 32'bz;  // Controlled_Buffer controlled_buffer_59
  assign controlled_buffer_2_out = decoder_3_out29[0] ? x29_q : 32'bz;  // Controlled_Buffer controlled_buffer_60
  assign controlled_buffer_1_out = decoder_2_out29[1] ? x30_q : 32'bz;  // Controlled_Buffer controlled_buffer_61
  assign controlled_buffer_2_out = decoder_3_out29[1] ? x30_q : 32'bz;  // Controlled_Buffer controlled_buffer_62
  assign controlled_buffer_1_out = decoder_2_out29[2] ? x31_q : 32'bz;  // Controlled_Buffer controlled_buffer_63
  assign controlled_buffer_2_out = decoder_3_out29[2] ? x31_q : 32'bz;  // Controlled_Buffer controlled_buffer_64
  Decoder #(.select(5)) decoder_2 (
    .out0(decoder_2_out0[0]), .out1(decoder_2_out0[1]), .out2(decoder_2_out0[2]), .out3(decoder_2_out0[3]),
    .out4(decoder_2_out0[4]), .out5(decoder_2_out5[0]), .out6(decoder_2_out5[1]), .out7(decoder_2_out5[2]),
    .out8(decoder_2_out8[0]), .out9(decoder_2_out8[1]), .out10(decoder_2_out8[2]), .out11(decoder_2_out8[3]),
    .out12(decoder_2_out8[4]), .out13(decoder_2_out13[0]), .out14(decoder_2_out13[1]),
    .out15(decoder_2_out13[2]), .out16(decoder_2_out16[0]), .out17(decoder_2_out16[1]),
    .out18(decoder_2_out16[2]), .out19(decoder_2_out16[3]), .out20(decoder_2_out16[4]),
    .out21(decoder_2_out21[0]), .out22(decoder_2_out21[1]), .out23(decoder_2_out21[2]),
    .out24(decoder_2_out24[0]), .out25(decoder_2_out24[1]), .out26(decoder_2_out24[2]),
    .out27(decoder_2_out24[3]), .out28(decoder_2_out24[4]), .out29(decoder_2_out29[0]),
    .out30(decoder_2_out29[1]), .out31(decoder_2_out29[2]), .sel(out_12[19:15]));  // open: en
  Decoder #(.select(5)) decoder_3 (
    .out0(decoder_3_out0[0]), .out1(decoder_3_out0[1]), .out2(decoder_3_out0[2]), .out3(decoder_3_out0[3]),
    .out4(decoder_3_out0[4]), .out5(decoder_3_out0[5]), .out6(decoder_3_out0[6]), .out7(decoder_3_out0[7]),
    .out8(decoder_3_out8[0]), .out9(decoder_3_out8[1]), .out10(decoder_3_out8[2]), .out11(decoder_3_out8[3]),
    .out12(decoder_3_out8[4]), .out13(decoder_3_out13[0]), .out14(decoder_3_out13[1]),
    .out15(decoder_3_out13[2]), .out16(decoder_3_out16[0]), .out17(decoder_3_out16[1]),
    .out18(decoder_3_out16[2]), .out19(decoder_3_out16[3]), .out20(decoder_3_out16[4]),
    .out21(decoder_3_out21[0]), .out22(decoder_3_out21[1]), .out23(decoder_3_out21[2]),
    .out24(decoder_3_out24[0]), .out25(decoder_3_out24[1]), .out26(decoder_3_out24[2]),
    .out27(decoder_3_out24[3]), .out28(decoder_3_out24[4]), .out29(decoder_3_out29[0]),
    .out30(decoder_3_out29[1]), .out31(decoder_3_out29[2]), .sel(out_12[24:20]));  // open: en
  Clock clock_5 (.out(clock_5_out));
  Register #(.width(32)) u_imm (.D(out_14), .en(1'b1), .Q(imm));  // open: clk, clr
  Register #(.width(32)) u_PC2 (.D(PC1), .en(1'b1), .clk(clock_5_out), .Q(PC2));  // open: clr
  Register #(.width(5)) u_rd0 (.D(out_12[11:7]), .en(1'b1), .clk(clock_5_out), .Q(rd0));  // open: clr
  Register #(.width(7)) u_op0 (.D(out_12[6:0]), .en(1'b1), .clk(clock_5_out), .Q(op0));  // open: clr
  Register #(.width(10)) u_funct (
    .D({out_12[31:25], out_12[14:12]}), .en(1'b1), .clk(clock_5_out), .Q(funct));  // open: clr
  Register #(.width(32)) u_S2 (.D(controlled_buffer_2_out), .en(1'b1), .clk(clock_5_out), .Q(S2));  // open: clr
  Register #(.width(32)) u_S1 (.D(controlled_buffer_1_out), .en(1'b1), .clk(clock_5_out), .Q(S1));  // open: clr

  assign out_13 = out_12[6:0];

  // Other names for the same wires on the sheet: funct3[2:0] = out_12[14:12];
  //   immJ[20:1] = {out_12[31], out_12[19:12], out_12[20], out_12[30:21]}; immU[31:12] = out_12[31:12];
  //   Instr[31:0] = out_12; funct7[6:0] = out_12[31:25];
  //   immB[12:1] = {out_12[31], out_12[7], out_12[30:25], out_12[11:8]}; immI[11:0] = out_12[31:20];
  //   immS[11:0] = {out_12[31:25], out_12[11:7]}; SE = out_12[31]; GateALU = in_10; GateMAR = in_8; GateMDR = in_9;
  //   GatePC = in_4; imm32[31:0] = out_14; rd[4:0] = out_12[11:7]; rs1[4:0] = out_12[19:15]; rs2[4:0] = out_12[24:20];
  //   opcode[6:0] = out_12[6:0]; LD_IR = in_6; LD_PC = in_5; LD_REG = in_7; PC[31:0] = out_11; PCMUX = in_3;
  //   ResetSim = in_2; SR1[31:0] = out_15; SR2[31:0] = out_16; testing = in_1

  // Notes on the sheet:
  //   R
  //   I
  //   S
  //   B
  //   U
  //   J
  //   DR
  //   REGISTER FILE
  //   SR1
  //   SR2
endmodule

module ALU (
  input  [31:0] A,
  input  [31:0] B,
  input  [2:0] OP,
  output [31:0] ALU_OUT,
  output [3:0] CNZV
);

  wire [31:0] adder_1_out, and_1_out, bit_extender_1_out, multiplexer_1_out, multiplexer_2_out, not_1_out,
       or_1_out, xor_1_out, xor_2_out;

  assign bit_extender_1_out = {{31{OP[2]}}, OP[2]};  // Bit_Extender bit_extender_1
  assign and_1_out = A & B;  // AND_Gate and_1, 32 bits wide
  assign or_1_out = A | B;  // OR_Gate or_1, 32 bits wide
  assign xor_1_out = A ^ B;  // XOR_Gate xor_1, 32 bits wide
  assign not_1_out = ~B;  // NOT_Gate not_1, 32 bits wide
  Multiplexer #(.width(32)) multiplexer_1 (.in0(A), .in1({32{1'b0}}), .out(multiplexer_1_out), .sel(OP[0]));
  assign xor_2_out = B ^ bit_extender_1_out;  // XOR_Gate xor_2, 32 bits wide
  Multiplexer #(.select(2), .width(32)) multiplexer_2 (
    .in0(and_1_out), .in1(or_1_out), .in2(xor_1_out), .in3(not_1_out), .out(multiplexer_2_out), .sel(OP[1:0]));
  Adder #(.width(32)) adder_1 (.a(multiplexer_1_out), .b(xor_2_out), .out(adder_1_out), .cin(OP[1]), .cout(CNZV[3]));
  Multiplexer #(.width(32)) multiplexer_3 (.in0(multiplexer_2_out), .in1(adder_1_out), .out(ALU_OUT), .sel(OP[2]));
  xor xor_3 (CNZV[0], CNZV[3], adder_1_out[31]);
  nor nor_1 (CNZV[1], ALU_OUT[31], ALU_OUT[30], ALU_OUT[29], ALU_OUT[28], ALU_OUT[27], ALU_OUT[26], ALU_OUT[25], ALU_OUT[24], ALU_OUT[23], ALU_OUT[22], ALU_OUT[21], ALU_OUT[20], ALU_OUT[19], ALU_OUT[18], ALU_OUT[17], ALU_OUT[16], ALU_OUT[15], ALU_OUT[14], ALU_OUT[13], ALU_OUT[12], ALU_OUT[11], ALU_OUT[10], ALU_OUT[9], ALU_OUT[8], ALU_OUT[7], ALU_OUT[6], ALU_OUT[5], ALU_OUT[4], ALU_OUT[3], ALU_OUT[2], ALU_OUT[1], ALU_OUT[0]);

  assign CNZV[2] = ALU_OUT[31];
endmodule

module FD (
  input  [6:0] opcode,
  output [2:0] format
);

  wire comparator_1_eq, comparator_2_eq, comparator_3_eq, comparator_4_eq, comparator_5_eq, comparator_6_eq,
       comparator_7_eq, comparator_8_eq, comparator_9_eq, or_1_out, or_2_out;

  Comparator #(.width(7)) comparator_1 (.a(opcode), .b(7'b0110011), .eq(comparator_1_eq));  // open: gt, lt
  Comparator #(.width(7)) comparator_2 (.a(opcode), .b(7'b0010011), .eq(comparator_2_eq));  // open: gt, lt
  Comparator #(.width(7)) comparator_3 (.a(opcode), .b(7'b0000011), .eq(comparator_3_eq));  // open: gt, lt
  Comparator #(.width(7)) comparator_4 (.a(opcode), .b(7'b1100111), .eq(comparator_4_eq));  // open: gt, lt
  Comparator #(.width(7)) comparator_5 (.a(opcode), .b(7'b0100011), .eq(comparator_5_eq));  // open: gt, lt
  Comparator #(.width(7)) comparator_6 (.a(opcode), .b(7'b1100011), .eq(comparator_6_eq));  // open: gt, lt
  Comparator #(.width(7)) comparator_7 (.a(opcode), .b(7'b0110111), .eq(comparator_7_eq));  // open: gt, lt
  Comparator #(.width(7)) comparator_8 (.a(opcode), .b(7'b0010111), .eq(comparator_8_eq));  // open: gt, lt
  Comparator #(.width(7)) comparator_9 (.a(opcode), .b(7'b1101111), .eq(comparator_9_eq));  // open: gt, lt
  or or_1 (or_1_out, comparator_2_eq, comparator_3_eq, comparator_4_eq);
  or or_2 (or_2_out, comparator_7_eq, comparator_8_eq);
  Priority_Encoder priority_encoder_1 (
    .in0(comparator_1_eq), .in1(or_1_out), .in2(comparator_5_eq), .in3(comparator_6_eq), .in4(or_2_out),
    .in5(comparator_9_eq), .out(format));  // open: in6, in7, en_in, gs, en_out

  // Notes on the sheet:
  //   R
  //   I
  //   S
  //   B
  //   U
  //   J
endmodule
